# Fritzing sketch IrrigationCircuit (saved by Fritzing 1.0.4)
breadboards: 1

parts:
  esp1 = ESP32 DevKitc V4
  S1 = Pushbutton [package=THT]
  RL1 = Solid State High Level Relay Module [package=relay]  # not connected
  RL2 = Solid State High Level Relay Module [package=relay]  # not connected
  RL4 = Solid State High Level Relay Module [package=relay]  # not connected
  RL3 = Solid State High Level Relay Module [package=relay]  # not connected
  RL5 = Solid State High Level Relay Module [package=relay]  # not connected
  RL6 = Solid State High Level Relay Module [package=relay]  # not connected
  RL8 = Solid State High Level Relay Module [package=relay]  # not connected
  RL7 = Solid State High Level Relay Module [package=relay]  # not connected
  S2 = Pushbutton [package=THT]
  S3 = Pushbutton [package=THT]
  S4 = Pushbutton [package=THT]
  S5 = Pushbutton [package=THT]
  S6 = Pushbutton [package=THT]
  S7 = Pushbutton [package=THT]
  S8 = Pushbutton [package=THT]
  S9 = Pushbutton [package=THT]
  RL9 = Solid State High Level Relay Module [package=relay]  # not connected

nets:
  N1: esp1.3V3, S1.leg1, S2.leg1, S3.leg1, S4.leg1, S5.leg1, S6.leg1, S7.leg1, S8.leg1, S9.leg1
  N2: esp1.VN, S1.leg0
  N3: esp1.IO34, S2.leg0
  N4: esp1.IO35, S3.leg0
  N5: esp1.IO32, S4.leg0
  N6: esp1.IO33, S5.leg0
  N7: esp1.IO25, S6.leg0
  N8: esp1.IO26, S7.leg0
  N9: esp1.IO27, S8.leg0
  N10: esp1.IO14, S9.leg0

custom parts:
  ESP32 DevKitc V4: ESP32-DevKitC board with ESP32-WROOM-32 module. ESP32-DevKitC V4 is a small-sized ESP32-based development board produced by Espressif. Most of the pins on the ESP module are broken out to the pin headers on the board. The pins D0, D1, D2, D3, CMD and CLK are used internally for communication between ESP32 and SPI flash memory. They are grouped on both sides near the USB connector. Avoid using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
  Solid State High Level Relay Module: 5V Omron solid state relay 240V 2A output with resistance fuse.
